# Fritzing sketch ArduinoMicro_Ribbon_CV (saved by Fritzing 0.9.2b)
breadboards: 1

parts:
  C1 = Ceramic Capacitor [capacitance=33nF voltage=10V package="100 mil [THT, multilayer]"]
  Part3 = Audio Jack Breakout
  IC1 = IC, DIP package, 14 pins [chip_label=MCP4922]
  C2 = Ceramic Capacitor [capacitance=100nF package="100 mil [THT, multilayer]"]
  Part1 = Arduino Micro (Rev3)
  Part4 = Audio Jack Breakout
  Part2 = Audio Jack Breakout

nets:
  GND: C1.0, Part3.GND, IC1.pin8, IC1.pin12, C2.0, Part1.GND, Part4.GND, Part2.GND
  N1: C1.1, Part1.A5, Part2.RING
  N2: Part3.RING, Part1.D5_PWM
  N3: Part3.TIP, IC1.pin14
  5V: IC1.pin1, IC1.pin9, IC1.pin11, IC1.pin13, C2.1, Part1.5V
  N4: IC1.pin3, Part1.D10_PWM/A10
  N5: IC1.pin4, Part1.SCK
  N6: IC1.pin5, Part1.MOSI
  N7: IC1.pin10, Part4.TIP

notes:
  PITCH CV OUT
  RIBBON INPUT
  TRIGGER OUT
  FILTER CV OUT
  Pitch CV Out
  Trigger Out
  Filter CV Out
  Ribbon Input
  DAC
  Arduino Ribbon CV Controller
  Arduino+DAC  Ribbon CV Controller
